# Fritzing sketch RoboFootball_model_electric (saved by Fritzing 0.9.3b)

parts:
  Часть1 = Arduino Uno (Rev3)
  Часть3 = IFR520 MOS module [package=THT]
  Power_plug1 = Power plug
  C1 = Electrolytic Capacitor [capacitance=4.7mF voltage=16V package="300 mil [THT, electrolytic]"]
  L2 = Solenoid

nets:
  N1: Часть1.D5_PWM, Часть3.pin1
  N2: Часть3.pin4, C1.+, L2.pin2
  N3: Часть3.pin5, C1.-, L2.pin1
  N4: Часть3.pin6, Power_plug1.VCC
  N5: Часть3.pin7, Power_plug1.GND

notes:
  12V
